// Logisim project RV32IM.circ as structural Verilog: 7 circuits, main circuit main
module CPU (
  input  [31:0] mem_read_data,
  input  [31:0] inst,
  input  [31:0] init_pc,
  input  clk,
  input  reset,
  output [31:0] mem_addr,
  output [31:0] reg_x3,
  output [31:0] mem_write_data,
  output [31:0] reg_x30,
  output mem_w_en,
  output [31:0] reg_x31,
  output mem_r_en,
  output [2:0] mem_data_type,
  output [31:0] PC
);

  wire and_1_out, and_2_out, and_3_out, and_4_out, and_5_out, and_6_out, B_beq, B_bge, B_bgeu, B_blt, B_bltu,
       B_bne, B_type, comparator_1_eq, comparator_2_eq, comparator_3_lt, comparator_4_lt, comparator_5_lt,
       comparator_6_lt, comparator_7_lt, comparator_17_eq, comparator_18_eq, comparator_19_eq,
       comparator_20_eq, comparator_21_eq, comparator_22_eq, comparator_23_eq, comparator_24_eq,
       comparator_25_eq, comparator_26_eq, comparator_27_eq, comparator_28_eq, comparator_29_eq,
       comparator_30_eq, comparator_31_eq, comparator_32_eq, comparator_33_eq, comparator_34_eq,
       comparator_35_eq, comparator_36_eq, comparator_37_eq, comparator_38_eq, comparator_39_eq,
       comparator_40_eq, comparator_41_eq, comparator_42_eq, comparator_43_eq, comparator_44_eq,
       comparator_45_eq, comparator_46_eq, comparator_47_eq, comparator_48_eq, comparator_49_eq,
       comparator_50_eq, comparator_51_eq, comparator_52_eq, comparator_53_eq, comparator_54_eq,
       comparator_55_eq, comparator_56_eq, comparator_57_eq, comparator_58_eq, comparator_59_eq,
       comparator_60_eq, comparator_61_eq, comparator_62_eq, comparator_63_eq, comparator_64_eq,
       comparator_65_eq, comparator_66_eq, comparator_67_eq, comparator_68_eq, comparator_69_eq,
       comparator_70_eq, I_addi, I_and, I_jalr, I_lb, I_lbu, I_lh, I_lhu, I_lw, I_ori, I_slli, I_slti,
       I_sltiu, I_srai, I_srli, I_type, I_type_arith, I_xori, J_type, or_1_out, or_2_out, or_3_out, or_4_out,
       or_8_out, or_9_out, or_10_out, or_11_out, or_12_out, or_13_out, or_14_out, or_15_out, or_16_out,
       or_17_out, or_18_out, or_19_out, R_add, R_and, R_div, R_mul, R_mulh, R_or, R_rem, R_sll, R_slt,
       R_sltu, R_sra, R_srl, R_sub, R_type, R_xor, reg_w_en, S_sb, S_sh, S_sw, U_lui, U_type, U_type_auipc;
  wire [1:0] priority_encoder_2_out, priority_encoder_3_out, priority_encoder_4_out;
  wire [2:0] priority_encoder_1_out, priority_encoder_6_out;
  wire [3:0] priority_encoder_5_out;
  wire [31:0] bit_extender_1_out, bit_extender_2_out, bit_extender_3_out, bit_extender_4_out,
       bit_extender_5_out, bit_extender_6_out, bit_extender_7_out, bit_extender_8_out, imm_value,
       multiplexer_1_out, multiplexer_2_out, multiplexer_3_out, multiplexer_4_out, multiplexer_6_out,
       PC_plus_4, r1_data, register_1_q;

  // Probe on inst
  Comparator #(.width(32)) comparator_1 (.a(r1_data), .b(mem_write_data), .eq(comparator_1_eq));  // open: gt, lt
  Comparator #(.width(32)) comparator_2 (.a(r1_data), .b(mem_write_data), .eq(comparator_2_eq));  // open: gt, lt
  Comparator #(.width(32)) comparator_3 (.a(r1_data), .b(mem_write_data), .lt(comparator_3_lt));  // open: gt, eq
  Comparator #(.width(32)) comparator_4 (.a(r1_data), .b(mem_write_data), .lt(comparator_4_lt));  // open: gt, eq
  Comparator #(.mode("unsigned"), .width(32)) comparator_5 (
    .a(r1_data), .b(mem_write_data), .lt(comparator_5_lt));  // open: gt, eq
  Comparator #(.mode("unsigned"), .width(32)) comparator_6 (
    .a(r1_data), .b(mem_write_data), .lt(comparator_6_lt));  // open: gt, eq
  assign bit_extender_1_out = {{24{mem_read_data[7]}}, mem_read_data[7:0]};  // Bit_Extender bit_extender_1
  assign bit_extender_2_out = {{16{mem_read_data[15]}}, mem_read_data[15:0]};  // Bit_Extender bit_extender_2
  assign bit_extender_3_out = {{24{1'b0}}, mem_read_data[7:0]};  // Bit_Extender bit_extender_3
  assign bit_extender_4_out = {{16{1'b0}}, mem_read_data[15:0]};  // Bit_Extender bit_extender_4
  or or_1 (or_1_out, R_type, I_type, mem_w_en);
  or or_2 (or_2_out, B_type, J_type, U_type_auipc);
  or or_3 (or_3_out, I_type, mem_w_en, B_type, U_type, J_type);
  and and_1 (and_1_out, B_beq, comparator_1_eq);
  and and_2 (and_2_out, B_bne, ~comparator_2_eq);  // AND_Gate
  and and_3 (and_3_out, B_blt, comparator_3_lt);
  and and_4 (and_4_out, B_bge, ~comparator_4_lt);  // AND_Gate
  and and_5 (and_5_out, B_bltu, comparator_5_lt);
  and and_6 (and_6_out, B_bgeu, ~comparator_6_lt);  // AND_Gate
  or or_4 (or_4_out, I_jalr, J_type);
  or or_5 (reg_w_en, R_type, I_type, U_type, J_type);
  Priority_Encoder priority_encoder_1 (
    .in0(I_lb), .in1(I_lh), .in2(I_lw), .in3(I_lbu), .in4(I_lhu), .out(priority_encoder_1_out));  // open: in5, in6, in7, en_in, gs, en_out
  Priority_Encoder #(.select(2)) priority_encoder_2 (
    .in0(or_1_out), .in1(or_2_out), .in2(U_lui), .out(priority_encoder_2_out));  // open: in3, gs, en_out, en_in
  Priority_Encoder #(.select(2)) priority_encoder_3 (
    .in0(R_type), .in1(or_3_out), .out(priority_encoder_3_out));  // open: in2, in3, gs, en_out, en_in
  Adder #(.width(32)) adder_1 (.a(PC), .b(32'h4), .out(PC_plus_4));  // open: cin, cout
  or or_6 (I_type, I_type_arith, mem_r_en, I_jalr);
  or or_7 (U_type, U_lui, U_type_auipc);
  Multiplexer #(.select(3), .width(32)) multiplexer_1 (
    .in0(bit_extender_1_out), .in1(bit_extender_2_out), .in2(mem_read_data), .in3(bit_extender_3_out),
    .in4(bit_extender_4_out), .out(multiplexer_1_out), .sel(priority_encoder_1_out));  // open: in5, in6, in7
  or or_8 (or_8_out, R_slt, I_slti);
  or or_9 (or_9_out, R_sltu, I_sltiu);
  Multiplexer #(.width(32)) multiplexer_2 (.in0(PC_plus_4), .in1(mem_addr), .out(multiplexer_2_out), .sel(or_10_out));
  or or_10 (or_10_out, and_1_out, and_2_out, and_3_out, and_4_out, and_5_out, and_6_out, or_4_out);
  assign bit_extender_5_out = {{20{inst[31]}}, inst[31:20]};  // Bit_Extender bit_extender_5
  assign bit_extender_6_out = {{20{inst[31]}}, {inst[31:25], inst[11:7]}};  // Bit_Extender bit_extender_6
  assign bit_extender_7_out = {{19{inst[31]}}, {inst[31], inst[7], inst[30:25], inst[11:8], 1'b0}};  // Bit_Extender bit_extender_7
  assign bit_extender_8_out = {{11{inst[31]}}, {inst[31], inst[19:12], inst[20], inst[30:21], 1'b0}};  // Bit_Extender bit_extender_8
  RegFile regfile_1 (
    .reg_w_en(reg_w_en), .clk(clk), .reset(reset), .reg_read_idx1(inst[19:15]), .reg_read_idx2(inst[24:20]),
    .reg_w_idx(inst[11:7]), .reg_write_data(multiplexer_6_out), .reg_read_data1(r1_data),
    .reg_read_data2(mem_write_data), .reg_x3(reg_x3), .reg_x30(reg_x30), .reg_x31(reg_x31));
  or or_11 (or_11_out, R_type, I_type_arith, U_type);
  or or_12 (or_12_out, J_type, I_jalr);
  Multiplexer #(.select(2), .width(32)) multiplexer_3 (
    .in0(mem_write_data), .in1(imm_value), .out(multiplexer_3_out), .sel(priority_encoder_3_out));  // open: in2, in3
  or or_13 (or_13_out, R_add, I_addi);
  or or_14 (or_14_out, R_and, I_and);
  or or_15 (or_15_out, R_or, I_ori);
  or or_16 (or_16_out, R_xor, I_xori);
  or or_17 (or_17_out, R_sll, I_slli);
  or or_18 (or_18_out, R_srl, I_srli);
  or or_19 (or_19_out, R_sra, I_srai);
  Register #(.width(32)) register_1 (.D(multiplexer_2_out), .en(1'b1), .clk(clk), .Q(register_1_q), .clr(reset));
  Priority_Encoder #(.select(2)) priority_encoder_4 (
    .in0(mem_r_en), .in1(or_11_out), .in2(or_12_out), .out(priority_encoder_4_out));  // open: in3, gs, en_out, en_in
  Multiplexer #(.select(2), .width(32)) multiplexer_4 (
    .in0(r1_data), .in1(PC), .in2({32{1'b0}}), .out(multiplexer_4_out), .sel(priority_encoder_2_out));  // open: in3
  Priority_Encoder #(.select(4)) priority_encoder_5 (
    .in0(or_13_out), .in1(R_sub), .in2(or_14_out), .in3(or_15_out), .in4(or_16_out), .in5(or_17_out),
    .in6(or_18_out), .in7(or_19_out), .in8(R_mul), .in9(R_mulh), .in10(R_div), .in11(R_rem), .in12(or_8_out),
    .in13(or_9_out), .out(priority_encoder_5_out));  // open: in14, in15, gs, en_out, en_in
  Multiplexer #(.select(3), .width(32)) multiplexer_5 (
    .in0(bit_extender_5_out), .in1(bit_extender_6_out), .in2(bit_extender_7_out),
    .in3({inst[31:12], {12{1'b0}}}), .in4(bit_extender_8_out), .out(imm_value), .sel(priority_encoder_6_out));  // open: in5, in6, in7
  Priority_Encoder priority_encoder_6 (
    .in0(I_type), .in1(mem_w_en), .in2(B_type), .in3(U_type), .in4(J_type), .out(priority_encoder_6_out));  // open: in5, in6, in7, en_in, gs, en_out
  Multiplexer #(.select(2), .width(32)) multiplexer_6 (
    .in0(multiplexer_1_out), .in1(mem_addr), .in2(PC_plus_4), .out(multiplexer_6_out),
    .sel(priority_encoder_4_out));  // open: in3
  Comparator #(.mode("unsigned"), .width(32)) comparator_7 (
    .a(register_1_q), .b(init_pc), .lt(comparator_7_lt));  // open: gt, eq
  ALU alu_1 (.A(multiplexer_4_out), .B(multiplexer_3_out), .OP(priority_encoder_5_out), .C(mem_addr));
  Multiplexer #(.width(32)) multiplexer_7 (.in0(register_1_q), .in1(init_pc), .out(PC), .sel(comparator_7_lt));
  Comparator #(.width(7)) comparator_8 (.a(inst[6:0]), .b(7'b0110011), .eq(R_type));  // open: gt, lt
  Comparator #(.width(7)) comparator_9 (.a(inst[6:0]), .b(7'b0010011), .eq(I_type_arith));  // open: gt, lt
  Comparator #(.width(7)) comparator_10 (.a(inst[6:0]), .b(7'b0000011), .eq(mem_r_en));  // open: gt, lt
  Comparator #(.width(7)) comparator_11 (.a(inst[6:0]), .b(7'b0100011), .eq(mem_w_en));  // open: gt, lt
  Comparator #(.width(7)) comparator_12 (.a(inst[6:0]), .b(7'b1100011), .eq(B_type));  // open: gt, lt
  Comparator #(.width(7)) comparator_13 (.a(inst[6:0]), .b(7'b1101111), .eq(J_type));  // open: gt, lt
  Comparator #(.width(7)) comparator_14 (.a(inst[6:0]), .b(7'b1100111), .eq(I_jalr));  // open: gt, lt
  Comparator #(.width(7)) comparator_15 (.a(inst[6:0]), .b(7'b0110111), .eq(U_lui));  // open: gt, lt
  Comparator #(.width(7)) comparator_16 (.a(inst[6:0]), .b(7'b0010111), .eq(U_type_auipc));  // open: gt, lt
  Comparator #(.width(3)) comparator_17 (.a(inst[14:12]), .b(3'b000), .eq(comparator_17_eq));  // open: gt, lt
  Comparator #(.width(7)) comparator_18 (.a(inst[31:25]), .b({7{1'b0}}), .eq(comparator_18_eq));  // open: gt, lt
  Comparator #(.width(3)) comparator_19 (.a(inst[14:12]), .b(3'b000), .eq(comparator_19_eq));  // open: gt, lt
  Comparator #(.width(7)) comparator_20 (.a(inst[31:25]), .b(7'b0000001), .eq(comparator_20_eq));  // open: gt, lt
  Comparator #(.width(3)) comparator_21 (.a(inst[14:12]), .b(3'b000), .eq(comparator_21_eq));  // open: gt, lt
  Comparator #(.width(7)) comparator_22 (.a(inst[31:25]), .b(7'b0100000), .eq(comparator_22_eq));  // open: gt, lt
  Comparator #(.width(3)) comparator_23 (.a(inst[14:12]), .b(3'b001), .eq(comparator_23_eq));  // open: gt, lt
  Comparator #(.width(7)) comparator_24 (.a(inst[31:25]), .b({7{1'b0}}), .eq(comparator_24_eq));  // open: gt, lt
  Comparator #(.width(3)) comparator_25 (.a(inst[14:12]), .b(3'b001), .eq(comparator_25_eq));  // open: gt, lt
  Comparator #(.width(7)) comparator_26 (.a(inst[31:25]), .b(7'b0000001), .eq(comparator_26_eq));  // open: gt, lt
  Comparator #(.width(3)) comparator_27 (.a(inst[14:12]), .b(3'b010), .eq(comparator_27_eq));  // open: gt, lt
  Comparator #(.width(7)) comparator_28 (.a(inst[31:25]), .b({7{1'b0}}), .eq(comparator_28_eq));  // open: gt, lt
  Comparator #(.width(3)) comparator_29 (.a(inst[14:12]), .b(3'b011), .eq(comparator_29_eq));  // open: gt, lt
  Comparator #(.width(7)) comparator_30 (.a(inst[31:25]), .b({7{1'b0}}), .eq(comparator_30_eq));  // open: gt, lt
  and and_7 (R_add, R_type, comparator_17_eq, comparator_18_eq);
  and and_8 (R_mul, R_type, comparator_19_eq, comparator_20_eq);
  and and_9 (R_sub, R_type, comparator_21_eq, comparator_22_eq);
  and and_10 (R_sll, R_type, comparator_23_eq, comparator_24_eq);
  and and_11 (R_mulh, R_type, comparator_25_eq, comparator_26_eq);
  and and_12 (R_slt, R_type, comparator_27_eq, comparator_28_eq);
  and and_13 (R_sltu, R_type, comparator_29_eq, comparator_30_eq);
  Comparator #(.width(3)) comparator_31 (.a(inst[14:12]), .b(3'b100), .eq(comparator_31_eq));  // open: gt, lt
  Comparator #(.width(7)) comparator_32 (.a(inst[31:25]), .b({7{1'b0}}), .eq(comparator_32_eq));  // open: gt, lt
  Comparator #(.width(3)) comparator_33 (.a(inst[14:12]), .b(3'b100), .eq(comparator_33_eq));  // open: gt, lt
  Comparator #(.width(7)) comparator_34 (.a(inst[31:25]), .b(7'b0000001), .eq(comparator_34_eq));  // open: gt, lt
  Comparator #(.width(3)) comparator_35 (.a(inst[14:12]), .b(3'b101), .eq(comparator_35_eq));  // open: gt, lt
  Comparator #(.width(7)) comparator_36 (.a(inst[31:25]), .b({7{1'b0}}), .eq(comparator_36_eq));  // open: gt, lt
  Comparator #(.width(3)) comparator_37 (.a(inst[14:12]), .b(3'b101), .eq(comparator_37_eq));  // open: gt, lt
  Comparator #(.width(7)) comparator_38 (.a(inst[31:25]), .b(7'b0100000), .eq(comparator_38_eq));  // open: gt, lt
  Comparator #(.width(3)) comparator_39 (.a(inst[14:12]), .b(3'b110), .eq(comparator_39_eq));  // open: gt, lt
  Comparator #(.width(7)) comparator_40 (.a(inst[31:25]), .b({7{1'b0}}), .eq(comparator_40_eq));  // open: gt, lt
  Comparator #(.width(3)) comparator_41 (.a(inst[14:12]), .b(3'b110), .eq(comparator_41_eq));  // open: gt, lt
  Comparator #(.width(7)) comparator_42 (.a(inst[31:25]), .b(7'b0000001), .eq(comparator_42_eq));  // open: gt, lt
  Comparator #(.width(3)) comparator_43 (.a(inst[14:12]), .b(3'b111), .eq(comparator_43_eq));  // open: gt, lt
  Comparator #(.width(7)) comparator_44 (.a(inst[31:25]), .b({7{1'b0}}), .eq(comparator_44_eq));  // open: gt, lt
  and and_14 (R_xor, R_type, comparator_31_eq, comparator_32_eq);
  and and_15 (R_div, R_type, comparator_33_eq, comparator_34_eq);
  and and_16 (R_srl, R_type, comparator_35_eq, comparator_36_eq);
  and and_17 (R_sra, R_type, comparator_37_eq, comparator_38_eq);
  and and_18 (R_or, R_type, comparator_39_eq, comparator_40_eq);
  and and_19 (R_rem, R_type, comparator_41_eq, comparator_42_eq);
  and and_20 (R_and, R_type, comparator_43_eq, comparator_44_eq);
  Comparator #(.width(3)) comparator_45 (.a(inst[14:12]), .b(3'b000), .eq(comparator_45_eq));  // open: gt, lt
  Comparator #(.width(3)) comparator_46 (.a(inst[14:12]), .b(3'b001), .eq(comparator_46_eq));  // open: gt, lt
  Comparator #(.width(3)) comparator_47 (.a(inst[14:12]), .b(3'b010), .eq(comparator_47_eq));  // open: gt, lt
  Comparator #(.width(3)) comparator_48 (.a(inst[14:12]), .b(3'b100), .eq(comparator_48_eq));  // open: gt, lt
  Comparator #(.width(3)) comparator_49 (.a(inst[14:12]), .b(3'b101), .eq(comparator_49_eq));  // open: gt, lt
  and and_21 (I_lb, mem_r_en, comparator_45_eq);
  and and_22 (I_lh, mem_r_en, comparator_46_eq);
  and and_23 (I_lw, mem_r_en, comparator_47_eq);
  and and_24 (I_lbu, mem_r_en, comparator_48_eq);
  and and_25 (I_lhu, mem_r_en, comparator_49_eq);
  Comparator #(.width(3)) comparator_50 (.a(inst[14:12]), .b(3'b000), .eq(comparator_50_eq));  // open: gt, lt
  Comparator #(.width(3)) comparator_51 (.a(inst[14:12]), .b(3'b100), .eq(comparator_51_eq));  // open: gt, lt
  Comparator #(.width(3)) comparator_52 (.a(inst[14:12]), .b(3'b110), .eq(comparator_52_eq));  // open: gt, lt
  Comparator #(.width(3)) comparator_53 (.a(inst[14:12]), .b(3'b111), .eq(comparator_53_eq));  // open: gt, lt
  Comparator #(.width(3)) comparator_54 (.a(inst[14:12]), .b(3'b001), .eq(comparator_54_eq));  // open: gt, lt
  Comparator #(.width(7)) comparator_55 (.a(inst[31:25]), .b({7{1'b0}}), .eq(comparator_55_eq));  // open: gt, lt
  Comparator #(.width(3)) comparator_56 (.a(inst[14:12]), .b(3'b101), .eq(comparator_56_eq));  // open: gt, lt
  Comparator #(.width(7)) comparator_57 (.a(inst[31:25]), .b({7{1'b0}}), .eq(comparator_57_eq));  // open: gt, lt
  Comparator #(.width(3)) comparator_58 (.a(inst[14:12]), .b(3'b101), .eq(comparator_58_eq));  // open: gt, lt
  Comparator #(.width(7)) comparator_59 (.a(inst[31:25]), .b(7'b0100000), .eq(comparator_59_eq));  // open: gt, lt
  Comparator #(.width(3)) comparator_60 (.a(inst[14:12]), .b(3'b010), .eq(comparator_60_eq));  // open: gt, lt
  Comparator #(.width(3)) comparator_61 (.a(inst[14:12]), .b(3'b011), .eq(comparator_61_eq));  // open: gt, lt
  and and_26 (I_addi, I_type_arith, comparator_50_eq);
  and and_27 (I_xori, I_type_arith, comparator_51_eq);
  and and_28 (I_ori, I_type_arith, comparator_52_eq);
  and and_29 (I_and, I_type_arith, comparator_53_eq);
  and and_30 (I_slli, I_type_arith, comparator_54_eq, comparator_55_eq);
  and and_31 (I_srli, I_type_arith, comparator_56_eq, comparator_57_eq);
  and and_32 (I_srai, I_type_arith, comparator_58_eq, comparator_59_eq);
  and and_33 (I_slti, I_type_arith, comparator_60_eq);
  and and_34 (I_sltiu, I_type_arith, comparator_61_eq);
  Comparator #(.width(3)) comparator_62 (.a(inst[14:12]), .b(3'b000), .eq(comparator_62_eq));  // open: gt, lt
  Comparator #(.width(3)) comparator_63 (.a(inst[14:12]), .b(3'b001), .eq(comparator_63_eq));  // open: gt, lt
  Comparator #(.width(3)) comparator_64 (.a(inst[14:12]), .b(3'b010), .eq(comparator_64_eq));  // open: gt, lt
  Comparator #(.width(3)) comparator_65 (.a(inst[14:12]), .b(3'b000), .eq(comparator_65_eq));  // open: gt, lt
  Comparator #(.width(3)) comparator_66 (.a(inst[14:12]), .b(3'b001), .eq(comparator_66_eq));  // open: gt, lt
  Comparator #(.width(3)) comparator_67 (.a(inst[14:12]), .b(3'b100), .eq(comparator_67_eq));  // open: gt, lt
  Comparator #(.width(3)) comparator_68 (.a(inst[14:12]), .b(3'b101), .eq(comparator_68_eq));  // open: gt, lt
  Comparator #(.width(3)) comparator_69 (.a(inst[14:12]), .b(3'b110), .eq(comparator_69_eq));  // open: gt, lt
  Comparator #(.width(3)) comparator_70 (.a(inst[14:12]), .b(3'b111), .eq(comparator_70_eq));  // open: gt, lt
  and and_35 (S_sb, mem_w_en, comparator_62_eq);
  and and_36 (S_sh, mem_w_en, comparator_63_eq);
  and and_37 (S_sw, mem_w_en, comparator_64_eq);
  and and_38 (B_beq, B_type, comparator_65_eq);
  and and_39 (B_bne, B_type, comparator_66_eq);
  and and_40 (B_blt, B_type, comparator_67_eq);
  and and_41 (B_bge, B_type, comparator_68_eq);
  and and_42 (B_bltu, B_type, comparator_69_eq);
  and and_43 (B_bgeu, B_type, comparator_70_eq);

  assign mem_data_type = inst[14:12];

  // Other names for the same wires on the sheet: rd_idx[4:0] = inst[11:7]; r2_idx[4:0] = inst[24:20];
  //   funct7[6:0] = inst[31:25]; funct3[2:0] = inst[14:12]; r1_idx[4:0] = inst[19:15]; alu_out[31:0] = mem_addr;
  //   I_type_jump = I_jalr; I_type_load = mem_r_en; opcode[6:0] = inst[6:0]; r2_data[31:0] = mem_write_data;
  //   S_type = mem_w_en; U_jal = J_type; U_type_load = U_lui

  // Notes on the sheet:
  //   I/O
  //   1.Fetch
  //   2.DECODE
  //   3. Registers
  //   5. Writeback
  //   4. Execute
  //   R-Type
  //   I-Type
  //   S-Type
  //   B-Type
  //   U-Type
  //   J-Type
  //   instRUCTION Parameterization
  //   Inputs
  //   imm[11:0]
  //   imm[4:0]
  //   imm[11:5]
  //   imm[11]
  //   imm[4:1]
  //   imm[10:5]
  //   imm[12]
  //   imm[31:12]
  //   imm[19:12]
  //   imm[11]
  //   imm[10:1]
  //   imm[20]
  //   Outputs
  //   Debug
  //   instruction decoding
endmodule

module RegFile (
  input  [4:0] reg_read_idx1,
  input  [4:0] reg_read_idx2,
  input  [4:0] reg_w_idx,
  input  [31:0] reg_write_data,
  input  reg_w_en,
  input  clk,
  input  reset,
  output [31:0] reg_read_data1,
  output [31:0] reg_read_data2,
  output [31:0] reg_x3,
  output [31:0] reg_x30,
  output [31:0] reg_x31
);

  wire we_1, we_2, we_3, we_4, we_5, we_6, we_7, we_8, we_9, we_10, we_11, we_12, we_13, we_14, we_15, we_16,
       we_17, we_18, we_19, we_20, we_21, we_22, we_23, we_24, we_25, we_26, we_27, we_28, we_29, we_30,
       we_31;
  wire [31:0] in_x1, in_x2, in_x3, in_x4, in_x5, in_x6, in_x7, in_x8, in_x9, in_x10, in_x11, in_x12, in_x13,
       in_x14, in_x15, in_x16, in_x17, in_x18, in_x19, in_x20, in_x21, in_x22, in_x23, in_x24, in_x25,
       in_x26, in_x27, in_x28, in_x29, in_x30, in_x31, out_x1, out_x2, out_x4, out_x5, out_x6, out_x7,
       out_x8, out_x9, out_x10, out_x11, out_x12, out_x13, out_x14, out_x15, out_x16, out_x17, out_x18,
       out_x19, out_x20, out_x21, out_x22, out_x23, out_x24, out_x25, out_x26, out_x27, out_x28, out_x29;

  Register #(.width(32)) ra (.D(in_x1), .en(we_1), .clk(clk), .Q(out_x1), .clr(reset));
  Register #(.width(32)) register_1 (.D(in_x9), .en(we_9), .clk(clk), .Q(out_x9), .clr(reset));
  Register #(.width(32)) register_2 (.D(in_x17), .en(we_17), .clk(clk), .Q(out_x17), .clr(reset));
  Register #(.width(32)) register_3 (.D(in_x25), .en(we_25), .clk(clk), .Q(out_x25), .clr(reset));
  Multiplexer #(.select(5), .width(32)) multiplexer_1 (
    .in0({32{1'b0}}), .in1(out_x1), .in2(out_x2), .in3(reg_x3), .in4(out_x4), .in5(out_x5), .in6(out_x6),
    .in7(out_x7), .in8(out_x8), .in9(out_x9), .in10(out_x10), .in11(out_x11), .in12(out_x12), .in13(out_x13),
    .in14(out_x14), .in15(out_x15), .in16(out_x16), .in17(out_x17), .in18(out_x18), .in19(out_x19),
    .in20(out_x20), .in21(out_x21), .in22(out_x22), .in23(out_x23), .in24(out_x24), .in25(out_x25),
    .in26(out_x26), .in27(out_x27), .in28(out_x28), .in29(out_x29), .in30(reg_x30), .in31(reg_x31),
    .out(reg_read_data1), .sel(reg_read_idx1));
  Register #(.width(32)) sp (.D(in_x2), .en(we_2), .clk(clk), .Q(out_x2), .clr(reset));
  Register #(.width(32)) a0 (.D(in_x10), .en(we_10), .clk(clk), .Q(out_x10), .clr(reset));
  Register #(.width(32)) register_4 (.D(in_x18), .en(we_18), .clk(clk), .Q(out_x18), .clr(reset));
  Register #(.width(32)) register_5 (.D(in_x26), .en(we_26), .clk(clk), .Q(out_x26), .clr(reset));
  Register #(.width(32)) gp (.D(in_x3), .en(we_3), .clk(clk), .Q(reg_x3), .clr(reset));
  Register #(.width(32)) register_6 (.D(in_x11), .en(we_11), .clk(clk), .Q(out_x11), .clr(reset));
  Register #(.width(32)) register_7 (.D(in_x19), .en(we_19), .clk(clk), .Q(out_x19), .clr(reset));
  Register #(.width(32)) register_8 (.D(in_x27), .en(we_27), .clk(clk), .Q(out_x27), .clr(reset));
  Multiplexer #(.select(5), .width(32)) multiplexer_2 (
    .in0({32{1'b0}}), .in1(out_x1), .in2(out_x2), .in3(reg_x3), .in4(out_x4), .in5(out_x5), .in6(out_x6),
    .in7(out_x7), .in8(out_x8), .in9(out_x9), .in10(out_x10), .in11(out_x11), .in12(out_x12), .in13(out_x13),
    .in14(out_x14), .in15(out_x15), .in16(out_x16), .in17(out_x17), .in18(out_x18), .in19(out_x19),
    .in20(out_x20), .in21(out_x21), .in22(out_x22), .in23(out_x23), .in24(out_x24), .in25(out_x25),
    .in26(out_x26), .in27(out_x27), .in28(out_x28), .in29(out_x29), .in30(reg_x30), .in31(reg_x31),
    .out(reg_read_data2), .sel(reg_read_idx2));
  Register #(.width(32)) register_9 (.D(in_x4), .en(we_4), .clk(clk), .Q(out_x4), .clr(reset));
  Register #(.width(32)) register_10 (.D(in_x12), .en(we_12), .clk(clk), .Q(out_x12), .clr(reset));
  Register #(.width(32)) register_11 (.D(in_x20), .en(we_20), .clk(clk), .Q(out_x20), .clr(reset));
  Register #(.width(32)) register_12 (.D(in_x28), .en(we_28), .clk(clk), .Q(out_x28), .clr(reset));
  Demultiplexer #(.enable("true"), .select(5), .width(32)) demultiplexer_1 (
    .out1(in_x1), .out2(in_x2), .out3(in_x3), .out4(in_x4), .out5(in_x5), .out6(in_x6), .out7(in_x7),
    .out8(in_x8), .out9(in_x9), .out10(in_x10), .out11(in_x11), .out12(in_x12), .out13(in_x13),
    .out14(in_x14), .out15(in_x15), .out16(in_x16), .out17(in_x17), .out18(in_x18), .out19(in_x19),
    .out20(in_x20), .out21(in_x21), .out22(in_x22), .out23(in_x23), .out24(in_x24), .out25(in_x25),
    .out26(in_x26), .out27(in_x27), .out28(in_x28), .out29(in_x29), .out30(in_x30), .out31(in_x31),
    .in(reg_write_data), .sel(reg_w_idx), .en(reg_w_en));  // open: out0
  Register #(.width(32)) t0 (.D(in_x5), .en(we_5), .clk(clk), .Q(out_x5), .clr(reset));
  Register #(.width(32)) register_13 (.D(in_x13), .en(we_13), .clk(clk), .Q(out_x13), .clr(reset));
  Register #(.width(32)) register_14 (.D(in_x21), .en(we_21), .clk(clk), .Q(out_x21), .clr(reset));
  Register #(.width(32)) register_15 (.D(in_x29), .en(we_29), .clk(clk), .Q(out_x29), .clr(reset));
  Register #(.width(32)) register_16 (.D(in_x6), .en(we_6), .clk(clk), .Q(out_x6), .clr(reset));
  Register #(.width(32)) register_17 (.D(in_x14), .en(we_14), .clk(clk), .Q(out_x14), .clr(reset));
  Register #(.width(32)) register_18 (.D(in_x22), .en(we_22), .clk(clk), .Q(out_x22), .clr(reset));
  Register #(.width(32)) register_19 (.D(in_x30), .en(we_30), .clk(clk), .Q(reg_x30), .clr(reset));
  Decoder #(.select(5)) decoder_1 (
    .out1(we_1), .out2(we_2), .out3(we_3), .out4(we_4), .out5(we_5), .out6(we_6), .out7(we_7), .out8(we_8),
    .out9(we_9), .out10(we_10), .out11(we_11), .out12(we_12), .out13(we_13), .out14(we_14), .out15(we_15),
    .out16(we_16), .out17(we_17), .out18(we_18), .out19(we_19), .out20(we_20), .out21(we_21), .out22(we_22),
    .out23(we_23), .out24(we_24), .out25(we_25), .out26(we_26), .out27(we_27), .out28(we_28), .out29(we_29),
    .out30(we_30), .out31(we_31), .sel(reg_w_idx), .en(reg_w_en));  // open: out0
  Register #(.width(32)) register_20 (.D(in_x7), .en(we_7), .clk(clk), .Q(out_x7), .clr(reset));
  Register #(.width(32)) register_21 (.D(in_x15), .en(we_15), .clk(clk), .Q(out_x15), .clr(reset));
  Register #(.width(32)) register_22 (.D(in_x23), .en(we_23), .clk(clk), .Q(out_x23), .clr(reset));
  Register #(.width(32)) register_23 (.D(in_x31), .en(we_31), .clk(clk), .Q(reg_x31), .clr(reset));
  Register #(.width(32)) register_24 (.D(in_x8), .en(we_8), .clk(clk), .Q(out_x8), .clr(reset));
  Register #(.width(32)) register_25 (.D(in_x16), .en(we_16), .clk(clk), .Q(out_x16), .clr(reset));
  Register #(.width(32)) register_26 (.D(in_x24), .en(we_24), .clk(clk), .Q(out_x24), .clr(reset));

  // Other names for the same wires on the sheet: out_x3[31:0] = reg_x3; out_x30[31:0] = reg_x30;
  //   out_x31[31:0] = reg_x31

  // Notes on the sheet:
  //   Inputs
  //   Register Reading
  //   Outputs
  //   Register Writing
endmodule

module ALU (
  input  [31:0] A,
  input  [31:0] B,
  input  [3:0] OP,
  output [31:0] C
);

  wire comparator_1_lt, comparator_2_lt;
  wire [31:0] adder_1_out, and_1_out, bit_extender_1_out, bit_extender_2_out, divider_1_out, divider_2_rem,
       multiplier_1_out, multiplier_2_cout, or_1_out, shifter_1_out, shifter_2_out, shifter_3_out,
       subtractor_1_out, xor_1_out;

  Adder #(.width(32)) adder_1 (.a(A), .b(B), .out(adder_1_out));  // open: cin, cout
  Subtractor #(.width(32)) subtractor_1 (.a(A), .b(B), .out(subtractor_1_out));  // open: bin, bout
  assign and_1_out = A & B;  // AND_Gate and_1, 32 bits wide
  assign or_1_out = A | B;  // OR_Gate or_1, 32 bits wide
  assign xor_1_out = A ^ B;  // XOR_Gate xor_1, 32 bits wide
  Shifter #(.width(32)) shifter_1 (.in(A), .\dist (B[4:0]), .out(shifter_1_out));
  Shifter #(.shift("lr"), .width(32)) shifter_2 (.in(A), .\dist (B[4:0]), .out(shifter_2_out));
  Shifter #(.shift("ar"), .width(32)) shifter_3 (.in(A), .\dist (B[4:0]), .out(shifter_3_out));
  Multiplier #(.width(32)) multiplier_1 (.a(A), .b(B), .out(multiplier_1_out));  // open: cin, cout
  Multiplier #(.width(32)) multiplier_2 (.a(A), .b(B), .cout(multiplier_2_cout));  // open: out, cin
  Divider #(.width(32)) divider_1 (.a(A), .b(B), .out(divider_1_out));  // open: upper, rem
  Divider #(.width(32)) divider_2 (.a(A), .b(B), .rem(divider_2_rem));  // open: out, upper
  Comparator #(.width(32)) comparator_1 (.a(A), .b(B), .lt(comparator_1_lt));  // open: gt, eq
  assign bit_extender_1_out = {{31{1'b0}}, comparator_1_lt};  // Bit_Extender bit_extender_1
  Comparator #(.mode("unsigned"), .width(32)) comparator_2 (.a(A), .b(B), .lt(comparator_2_lt));  // open: gt, eq
  assign bit_extender_2_out = {{31{1'b0}}, comparator_2_lt};  // Bit_Extender bit_extender_2
  Multiplexer #(.select(4), .width(32)) multiplexer_1 (
    .in0(adder_1_out), .in1(subtractor_1_out), .in2(and_1_out), .in3(or_1_out), .in4(xor_1_out),
    .in5(shifter_1_out), .in6(shifter_2_out), .in7(shifter_3_out), .in8(multiplier_1_out),
    .in9(multiplier_2_cout), .in10(divider_1_out), .in11(divider_2_rem), .in12(bit_extender_1_out),
    .in13(bit_extender_2_out), .out(C), .sel(OP));  // open: in14, in15

  // Notes on the sheet:
  //   add
  //   sub
  //   and
  //   or
  //   xor
  //   sll
  //   srl
  //   sra
  //   mul
  //   mulh
  //   div
  //   rem
  //   slt
  //   sltu
  //   Outputs
  //   I/O
  //   Inputs
endmodule

module main (
);

  wire clk, keyboard_1_avail, keyboardctrl_1_kb_clear, keyboardctrl_1_kb_pop, keyboardctrl_1_kb_w_en,
       mem_r_en, mem_w_en, reset, ttyctrl_1_tty_clear, ttyctrl_1_tty_w_en;
  wire [2:0] mem_data_type;
  wire [3:0] memctrl_1_bytes_enable;
  wire [6:0] keyboard_1_data, ttyctrl_1_tty_wdata;
  wire [31:0] cpu_1_reg_x30, cpu_1_reg_x31, IMEM_data, mem_addr, mem_base_addr, mem_read_data,
       mem_write_data, memctrl_1_word_addr, memctrl_1_word_wdata, PC, ram_1_dout, shifter_1_out,
       subtractor_1_out;

  MemCtrl memctrl_1 (
    .addr(mem_addr), .base_addr(mem_base_addr), .size(32'h40000), .data_type(mem_data_type),
    .word_rdata(ram_1_dout), .wdata(mem_write_data), .rdata(mem_read_data), .word_addr(memctrl_1_word_addr),
    .bytes_enable(memctrl_1_bytes_enable), .word_wdata(memctrl_1_word_wdata));
  Button u_reset (.out(reset));
  CPU cpu_1 (
    .mem_read_data(mem_read_data), .inst(IMEM_data), .init_pc(32'h80000000), .clk(clk), .reset(reset),
    .mem_addr(mem_addr), .mem_write_data(mem_write_data), .mem_w_en(mem_w_en), .mem_r_en(mem_r_en),
    .mem_data_type(mem_data_type), .PC(PC), .reg_x3(mem_base_addr), .reg_x30(cpu_1_reg_x30),
    .reg_x31(cpu_1_reg_x31));
  // Probe on mem_read_data
  Clock u_clk (.out(clk));
  RAM #(.addrWidth(16), .asyncread("true"), .byteenables("byteEnables"), .clearpin("true"), .dataWidth(32)) ram_1 (
    .addr(memctrl_1_word_addr[15:0]), .we(mem_w_en), .oe(mem_r_en), .clk(clk), .din(memctrl_1_word_wdata),
    .dout(ram_1_dout), .clr(reset), .be3(memctrl_1_bytes_enable[3]), .be2(memctrl_1_bytes_enable[2]),
    .be1(memctrl_1_bytes_enable[1]), .be0(memctrl_1_bytes_enable[0]));
  // Probe on cpu_1_reg_x30
  // Probe on cpu_1_reg_x31
  // Probe on mem_base_addr
  Subtractor #(.width(32)) subtractor_1 (.a(PC), .b(32'h80000000), .out(subtractor_1_out));  // open: bin, bout
  Shifter #(.shift("lr"), .width(32)) shifter_1 (.in(subtractor_1_out), .\dist (5'b00010), .out(shifter_1_out));
  TTYCtrl ttyctrl_1 (
    .addr(mem_addr), .wdata(mem_write_data), .w_en(mem_w_en), .base_addr(32'h1000), .reset(reset), .clk(clk),
    .tty_wdata(ttyctrl_1_tty_wdata), .tty_w_en(ttyctrl_1_tty_w_en), .tty_clear(ttyctrl_1_tty_clear));
  ROM #(.addrWidth(16), .dataWidth(32)) IMEM (.addr(shifter_1_out[15:0]), .data(IMEM_data));
  TTY tty_1 (.data(ttyctrl_1_tty_wdata), .clk(clk), .we(ttyctrl_1_tty_w_en), .clr(ttyctrl_1_tty_clear));
  Keyboard keyboard_1 (
    .clk(keyboardctrl_1_kb_pop), .re(keyboardctrl_1_kb_w_en), .clr(keyboardctrl_1_kb_clear),
    .avail(keyboard_1_avail), .data(keyboard_1_data));
  KeyboardCtrl keyboardctrl_1 (
    .waddr(mem_addr), .wdata(mem_write_data), .w_en(mem_w_en), .base_addr(32'h2000),
    .kb_available(keyboard_1_avail), .kb_data(keyboard_1_data), .reset(reset), .clk(clk),
    .kb_pop(keyboardctrl_1_kb_pop), .kb_w_en(keyboardctrl_1_kb_w_en), .kb_clear(keyboardctrl_1_kb_clear),
    .rdata(mem_read_data));
  // RGB_Video #(.height(256), .scale(1), .width(256)) rgb_video_1: pin names not known

  // Notes on the sheet:
  //   RISC-V Computer (RV32IM)
  //   Emin FEDAR | 2020
  //   Modified by DaleyDeng | 2023
  //   init_pc
  //   contents of IMEM (hex, n*v repeats v):
  //   8197 95818193 a800eef f13 f93 26800eef b906eef 28807eef 17003eef 1d100eef 19404eef 7006eef 905eef
  //   16d04eef 33005eef 72800eef 72c07eef 61803eef 66d00eef 6c804eef 5d806eef 58905eef 61904eef 9005eef
  //   7401eef 78101eef 1b901eef 33001eef 47901eef 65001eef 39002eef 60002eef 7102eef 31102eef 63502eef
  //   7b403eef 42d03eef 50506eef 21802eef 27002eef 5b502eef 7dd00eef 100f8f93 6f 8e17 8c0e0e13 ff00db7
  //   ffd8d93 1be2023 d93 1be2223 d93 1be2423 d93 1be2623 ff00db7 ffd8d93 1be2823 d93 1be2a23 d93 1be2c23
  //   d93 1be2e23 ff000db7 ffd8d93 3be2023 f00f1db7 ff0d8d93 3be2223 d93 3be2423 d93 3be2623 ff000db7
  //   ffd8d93 3be2823 f00f1db7 ff0d8d93 3be2a23 d93 3be2c23 d93 3be2e23 ff0db7 ffd8d93 5be2023 ff010db7
  //   f00d8d93 5be2223 ff01db7 ff0d8d93 5be2423 f00ffdb7 fd8d93 5be2623 efeffdb7 fefd8d93 5be2823 efeffdb7
  //   fefd8d93 5be2a23 fdb7 fefd8d93 5be2c23 d93 5be2e23 beefcdb7 eefd8d93 7be2023 beefcdb7 eefd8d93
  //   7be2223 beefcdb7 eefd8d93 7be2423 beefcdb7 eefd8d93 7be2623 beefcdb7 eefd8d93 7be2823 d93 7be2a23
  //   d93 7be2c23 d93 7be2e23 deadcdb7 eefd8d93 9be2023 deadcdb7 eefd8d93 9be2223 deadcdb7 eefd8d93
  //   9be2423 deadcdb7 eefd8d93 9be2623 deadcdb7 eefd8d93 9be2823 deadcdb7 eefd8d93 9be2a23 deadcdb7
  //   eefd8d93 9be2c23 deadcdb7 eefd8d93 9be2e23 deadcdb7 eefd8d93 bbe2023 deadcdb7 eefd8d93 bbe2223 e8067
  //   200f13 93 113 208733 393 4c771863 300f13 100093 100113 208733 200393 4a771c63 400f13 300093 700113
  //   208733 a00393 4a771063 500f13 93 ffff8137 208733 ffff83b7 48771463 600f13 800000b7 113 208733
  //   800003b7 46771863 700f13 800000b7 ffff8137 208733 7fff83b7 44771c63 800f13 93 8137 fff10113 208733
  //   83b7 fff38393 42771c63 900f13 800000b7 fff08093 113 208733 800003b7 fff38393 40771c63 a00f13
  //   800000b7 fff08093 8137 fff10113 208733 800083b7 ffe38393 3e771a63 b00f13 800000b7 8137 fff10113
  //   208733 800083b7 fff38393 3c771a63 c00f13 800000b7 fff08093 ffff8137 208733 7fff83b7 fff38393
  //   3a771a63 d00f13 93 fff00113 208733 fff00393 38771e63 e00f13 fff00093 100113 208733 393 38771263
  //   f00f13 fff00093 fff00113 208733 ffe00393 36771663 1000f13 100093 80000137 fff10113 208733 800003b7
  //   34771863 1100f13 d00093 b00113 2080b3 1800393 32709c63 1200f13 e00093 b00113 208133 1900393 32711063
  //   1300f13 d00093 1080b3 1a00393 30709663 1400f13 213 d00093 b00113 208733 70313 120213 200293 fe5214e3
  //   1800393 2e731063 1500f13 213 e00093 b00113 208733 13 70313 120213 200293 fe5212e3 1900393 2a731863
  //   1600f13 213 f00093 b00113 208733 13 13 70313 120213 200293 fe5210e3 1a00393 26731e63 1700f13 213
  //   d00093 b00113 208733 120213 200293 fe5216e3 1800393 24771a63 1800f13 213 e00093 b00113 13 208733
  //   120213 200293 fe5214e3 1900393 22771463 1900f13 213 f00093 b00113 13 13 208733 120213 200293
  //   fe5212e3 1a00393 1e771c63 1a00f13 213 d00093 13 b00113 208733 120213 200293 fe5214e3 1800393
  //   1c771663 1b00f13 213 e00093 13 b00113 13 208733 120213 200293 fe5212e3 1900393 18771e63 1c00f13 213
  //   f00093 13 13 b00113 208733 120213 200293 fe5212e3 1a00393 16771663 1d00f13 213 b00113 d00093 208733
  //   120213 200293 fe5216e3 1800393 14771263 1e00f13 213 b00113 e00093 13 208733 120213 200293 fe5214e3
  //   1900393 10771c63 1f00f13 213 b00113 f00093 13 13 208733 120213 200293 fe5212e3 1a00393 e771463
  //   2000f13 213 b00113 13 d00093 208733 120213 200293 fe5214e3 1800393 a771e63 2100f13 213 b00113 13
  //   e00093 13 208733 120213 200293 fe5212e3 1900393 8771663 2200f13 213 b00113 13 13 f00093 208733
  //   120213 200293 fe5212e3 1a00393 4771e63 2300f13 f00093 100133 f00393 4711463 2400f13 2000093 8133
  //   2000393 2711a63 2500f13 b3 393 2709263 2600f13 1000093 1e00113 208033 393 701663 1f8f93 e8067 6f
  //   200f13 93 8713 393 26771e63 300f13 100093 108713 200393 26771463 400f13 300093 708713 a00393
  //   24771a63 500f13 93 80008713 80000393 24771063 600f13 800000b7 8713 800003b7 22771663 700f13 800000b7
  //   80008713 800003b7 80038393 20771a63 800f13 93 7ff08713 7ff00393 20771063 900f13 800000b7 fff08093
  //   8713 800003b7 fff38393 1e771263 a00f13 800000b7 fff08093 7ff08713 800003b7 7fe38393 1c771463 b00f13
  //   800000b7 7ff08713 800003b7 7ff38393 1a771863 c00f13 800000b7 fff08093 80008713 7ffff3b7 7ff38393
  //   18771a63 d00f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
  //   tty
  //   keyboard
endmodule

module MemCtrl (
  input  [31:0] addr,
  input  [31:0] base_addr,
  input  [31:0] size,
  input  [2:0] data_type,
  input  [31:0] word_rdata,
  input  [31:0] wdata,
  output [31:0] rdata,
  output [31:0] word_addr,
  output [3:0] bytes_enable,
  output [31:0] word_wdata
);

  wire en, not_1_out;
  wire [3:0] decoder_1_out0, multiplexer_1_out, multiplexer_2_out, undriven;
  wire [4:0] bit_extender_1_out, multiplier_1_out;
  wire [31:0] multiplexer_3_out, real_addr, shifter_3_out, shifter_4_out;

  Subtractor #(.width(32)) subtractor_1 (.a(addr), .b(base_addr), .out(real_addr));  // open: bin, bout
  Multiplexer #(.select(2), .width(4)) multiplexer_1 (
    .in0(4'b0011), .in1(4'b0110), .in2(4'b1100), .in3(undriven), .out(multiplexer_1_out), .sel(real_addr[1:0]));
  // NoConnect on undriven
  Decoder #(.select(2)) decoder_1 (
    .out0(decoder_1_out0[0]), .out1(decoder_1_out0[1]), .out2(decoder_1_out0[2]), .out3(decoder_1_out0[3]),
    .sel(real_addr[1:0]));  // open: en
  assign bit_extender_1_out = {{3{1'b0}}, real_addr[1:0]};  // Bit_Extender bit_extender_1
  Multiplier #(.width(5)) multiplier_1 (
    .a(bit_extender_1_out), .b(5'b01000), .out(multiplier_1_out));  // open: cin, cout
  Shifter #(.shift("lr"), .width(32)) shifter_1 (.in(real_addr), .\dist (5'b00010), .out(word_addr));
  Comparator #(.mode("unsigned"), .width(32)) comparator_1 (.a(real_addr), .b(size), .lt(en));  // open: gt, eq
  Shifter #(.width(32)) shifter_2 (.in(wdata), .\dist (multiplier_1_out), .out(word_wdata));
  Shifter #(.shift("ar"), .width(32)) shifter_3 (.in(word_rdata), .\dist (multiplier_1_out), .out(shifter_3_out));
  Shifter #(.shift("lr"), .width(32)) shifter_4 (.in(word_rdata), .\dist (multiplier_1_out), .out(shifter_4_out));
  Multiplexer #(.select(2), .width(4)) multiplexer_2 (
    .in0(decoder_1_out0), .in1(multiplexer_1_out), .in2(4'b1111), .in3(4'b0000), .out(multiplexer_2_out),
    .sel(data_type[1:0]));
  Multiplexer #(.width(32)) multiplexer_3 (
    .in0(shifter_3_out), .in1(shifter_4_out), .out(multiplexer_3_out), .sel(data_type[2]));
  Multiplexer #(.width(4)) multiplexer_4 (.in0(4'b0000), .in1(multiplexer_2_out), .out(bytes_enable), .sel(en));
  not not_1 (not_1_out, en);
  // Transmission_Gate #(.width(32)) transmission_1: pin names not known; wires that end beside it: multiplexer_3_out, not_1_out, en, rdata

  // Other names for the same wires on the sheet: is_unsigned = data_type[2]
endmodule

module TTYCtrl (
  input  [31:0] addr,
  input  [31:0] wdata,
  input  w_en,
  input  [31:0] base_addr,
  input  reset,
  input  clk,
  output [6:0] tty_wdata,
  output tty_w_en,
  output tty_clear
);

  wire and_1_out, and_2_out, and_3_out, comparator_1_eq, comparator_2_eq, comparator_3_eq, multiplexer_1_out,
       multiplexer_3_out, undriven;
  wire [31:0] adder_1_out, adder_2_out;

  Adder #(.width(32)) adder_1 (.a(base_addr), .b(32'h2), .out(adder_1_out), .cin(undriven));  // open: cout
  Comparator #(.mode("unsigned"), .width(32)) comparator_1 (
    .a(addr), .b(adder_2_out), .eq(comparator_1_eq));  // open: gt, lt
  Adder #(.width(32)) adder_2 (.a(base_addr), .b(32'h1), .out(adder_2_out));  // open: cin, cout
  Comparator #(.mode("unsigned"), .width(32)) comparator_2 (
    .a(addr), .b(adder_1_out), .eq(comparator_2_eq));  // open: gt, lt
  Comparator #(.mode("unsigned"), .width(32)) comparator_3 (
    .a(addr), .b(base_addr), .eq(comparator_3_eq));  // open: gt, lt
  Multiplexer multiplexer_1 (.in0(tty_w_en), .in1(wdata[0]), .out(multiplexer_1_out), .sel(and_1_out));
  and and_1 (and_1_out, w_en, comparator_1_eq);
  Multiplexer #(.width(7)) multiplexer_2 (.in0({7{1'b0}}), .in1(wdata[6:0]), .out(tty_wdata), .sel(and_2_out));
  and and_2 (and_2_out, w_en, comparator_3_eq);
  D_Flip_Flop d_ff_1 (.D(multiplexer_1_out), .clk(clk), .Q(tty_w_en), .reset(reset));  // open: Qn, preset
  Multiplexer multiplexer_3 (.in0(1'b0), .in1(wdata[0]), .out(multiplexer_3_out), .sel(and_3_out));
  and and_3 (and_3_out, w_en, comparator_2_eq);
  or or_1 (tty_clear, multiplexer_3_out, reset);
endmodule

module KeyboardCtrl (
  input  [31:0] waddr,
  input  [31:0] wdata,
  input  w_en,
  input  [31:0] base_addr,
  input  kb_available,
  input  [6:0] kb_data,
  input  reset,
  input  clk,
  output kb_pop,
  output kb_w_en,
  output kb_clear,
  output [31:0] rdata
);

  wire and_1_out, and_2_out, and_3_out, and_4_out, comparator_1_eq, comparator_2_eq, comparator_3_eq,
       comparator_4_eq, multiplexer_1_out;
  wire [31:0] adder_1_out, adder_2_out, adder_3_out, bit_extender_1_out;

  Adder #(.width(32)) adder_1 (.a(base_addr), .b(32'h1), .out(adder_1_out));  // open: cin, cout
  Adder #(.width(32)) adder_2 (.a(base_addr), .b(32'h2), .out(adder_2_out));  // open: cin, cout
  Comparator #(.mode("unsigned"), .width(32)) comparator_1 (
    .a(waddr), .b(adder_1_out), .eq(comparator_1_eq));  // open: gt, lt
  and and_1 (and_1_out, w_en, comparator_1_eq);
  and and_2 (and_2_out, w_en, comparator_2_eq);
  Comparator #(.mode("unsigned"), .width(32)) comparator_2 (
    .a(waddr), .b(adder_2_out), .eq(comparator_2_eq));  // open: gt, lt
  D_Flip_Flop d_ff_1 (.D(multiplexer_1_out), .clk(clk), .Q(kb_w_en), .reset(reset));  // open: Qn, preset
  Multiplexer multiplexer_1 (.in0(kb_w_en), .in1(wdata[0]), .out(multiplexer_1_out), .sel(and_1_out));
  Multiplexer multiplexer_2 (.in0(1'b0), .in1(wdata[0]), .out(kb_pop), .sel(and_2_out));
  Adder #(.width(32)) adder_3 (.a(base_addr), .b(32'h3), .out(adder_3_out));  // open: cin, cout
  Comparator #(.mode("unsigned"), .width(32)) comparator_3 (
    .a(waddr), .b(base_addr), .eq(comparator_3_eq));  // open: gt, lt
  Comparator #(.mode("unsigned"), .width(32)) comparator_4 (
    .a(waddr), .b(adder_3_out), .eq(comparator_4_eq));  // open: gt, lt
  and and_3 (and_3_out, ~w_en, comparator_3_eq);  // AND_Gate
  Multiplexer multiplexer_3 (.in0(1'b0), .in1(wdata[0]), .out(kb_clear), .sel(and_4_out));
  and and_4 (and_4_out, w_en, comparator_4_eq);
  // NOT_Gate not_1 has open pins: in=and_3_out, out=open
  assign bit_extender_1_out = {{24{1'b0}}, {kb_available, kb_data}};  // Bit_Extender bit_extender_1
  // Transmission_Gate #(.width(32)) transmission_1: pin names not known; wires that end beside it: bit_extender_1_out, and_3_out, rdata

  // Other names for the same wires on the sheet: addr[31:0] = waddr
endmodule
